# Fritzing sketch Untitled Sketch (saved by Fritzing 0.9.2b)
breadboards: 1

parts:
  元件1 = Arduino Uno (Rev3)
  U1 = LCD-16X2 [package=lcd-8x2]
  U2 = PCF8574 [package="DIP16 [THT]"]
  J1 = Basic Servo

nets:
  N1: 元件1.D10_PWM/SS, J1.pulse
  GND: 元件1.GND, U2.GND, J1.gnd
  N2: 元件1.A4/SDA, U2.SDA
  N3: 元件1.A5/SCL, U2.SCL
  VCC: 元件1.5V, U2.VCC, J1.vcc
  N4: U1.RS, U2.P0
  N5: U1.R_W, U2.P1
  N6: U1.E, U2.P2
  N7: U1.DB3, U2.P3
  N8: U1.DB4, U2.P4
  N9: U1.DB5, U2.P5
  N10: U1.DB6, U2.P6
  N11: U1.DB7, U2.P7
